# Fritzing sketch Fiber_tower_circuit (saved by Fritzing 0.9.3b)
breadboards: 1

parts:
  Arduino = Arduino Uno (Rev3)
  M1 = Stepper Motor - Bipolar
  M2 = Stepper Motor - Bipolar
  Keyence_24v_power_source = Power plug
  Laser_sensor = mystery part, 4 pins [chip_label="Laser sensor"]
  Pot_2 = POT [package=alps_pot]
  Pot_1 = POT [package=alps_pot]
  Driver_3 = mystery part, 10 pins [chip_label=DM542T]
  M3 = Stepper Motor - Bipolar
  Driver_1 = mystery part, 10 pins [chip_label=DM542T]
  Driver_2 = mystery part, 10 pins [chip_label=DM542T]
  U1 = RELAY [package=relay-jzc]
  U2 = RELAY [package=relay-jzc]
  U3 = mystery part, 2 pins [chip_label=Oven]
  LED1 = smd LED [color="Red (633nm)" package="1206 [SMD]"]
  LED2 = smd LED [color="Red (633nm)" package="1206 [SMD]"]
  R1 = Resistor [tolerance=±5% resistance=220 package="0805 [SMD]"]
  R2 = Resistor [tolerance=±5% resistance=220 package="0805 [SMD]"]
  U4 = RELAY [package=relay-jzc]
  U5 = RELAY [package=relay-jzc]

nets:
  N1: Arduino.A0, Pot_1.S
  N2: Arduino.A1, Pot_2.S
  N3: Arduino.A2, Laser_sensor.pin3
  N4: Arduino.D10_PWM/SS, Driver_1.pin10
  N5: Arduino.D11_PWM/MOSI, Driver_1.pin8
  GND: Arduino.GND, Keyence_24v_power_source.GND, Laser_sensor.pin1, Laser_sensor.pin4, Pot_2.E, Pot_1.E, U1.COIL1, U2.COIL1, R1.Pin_1, R2.Pin_1, U4.NO, U4.COIL1, U5.COIL1
  N6: Arduino.D2, U4.COIL2, U5.COIL2
  N7: Arduino.D3_PWM, U1.COIL2, U2.COIL2
  N8: Arduino.D4, Driver_2.pin10
  N9: Arduino.D5_PWM, Driver_2.pin8
  N10: Arduino.D6_PWM, Driver_3.pin10
  N11: Arduino.D7, Driver_3.pin8
  N12: Arduino.5V, Pot_2.A, Pot_1.A, U2.MAIN, U5.MAIN
  N13: M1.A, Driver_1.pin4
  N14: M1.C, Driver_1.pin3
  N15: M1.B, Driver_1.pin2
  N16: M1.D, Driver_1.pin1
  N17: M2.A, Driver_2.pin4
  N18: M2.C, Driver_2.pin3
  N19: M2.B, Driver_2.pin2
  N20: M2.D, Driver_2.pin1
  N21: Keyence_24v_power_source.VCC, Laser_sensor.pin2, Driver_3.pin6, Driver_1.pin6, Driver_2.pin6
  N22: Driver_3.pin1, M3.D
  N23: Driver_3.pin2, M3.B
  N24: Driver_3.pin3, M3.C
  N25: Driver_3.pin4, M3.A
  N26: Driver_3.pin5, Driver_3.pin7, Driver_3.pin9, Driver_1.pin5, Driver_1.pin7, Driver_1.pin9, Driver_2.pin5, Driver_2.pin7, Driver_2.pin9, U4.MAIN
  N27: U1.NC, U3.pin1
  N28: U1.MAIN, U3.pin2
  N29: U2.NC, LED1.anode
  N30: LED1.cathode, R2.Pin_0
  N31: LED2.cathode, R1.Pin_0
  N32: LED2.anode, U5.NC
